// Logisim project nand2tetris.circ as structural Verilog
module my_or (
  input  ain,
  input  bin,
  output myout
);

  wire nand_1_out, nand_2_out;

  nand nand_1 (nand_1_out, ain, ain);
  nand nand_2 (nand_2_out, bin, bin);
  nand nand_3 (myout, nand_1_out, nand_2_out);
endmodule

module my_not (
  input  myin,
  output myout
);

  nand nand_1 (myout, myin, myin);
endmodule

module my_and (
  input  a,
  input  b,
  output MyOut
);

  wire nand_1_out, nand_2_out;

  nand nand_1 (nand_1_out, a, b);
  nand nand_2 (nand_2_out, a, b);
  nand nand_3 (MyOut, nand_1_out, nand_2_out);
endmodule

module my_XOR (
  input  a,
  input  b,
  output MyOut
);

  wire and_1_out, and_2_out, not_1_out, not_2_out;

  not not_1 (not_1_out, a);
  not not_2 (not_2_out, b);
  and and_1 (and_1_out, not_1_out, b);
  and and_2 (and_2_out, a, not_2_out);
  or or_1 (MyOut, and_1_out, and_2_out);
endmodule

module Mux (
  input  a,
  input  b,
  input  sel,
  output MyOut
);

  wire and_1_out, and_2_out, and_3_out, not_1_out, or_1_out;

  and and_1 (and_1_out, a, b);
  and and_2 (and_2_out, b, sel);
  and and_3 (and_3_out, a, not_1_out);
  not not_1 (not_1_out, sel);
  or or_1 (or_1_out, and_1_out, and_2_out);
  or or_2 (MyOut, or_1_out, and_3_out);
endmodule

module DMux (
  input  MyIn,
  input  sel,
  output a,
  output b
);

  wire not_1_out;

  not not_1 (not_1_out, sel);
  and and_1 (a, MyIn, not_1_out);
  and and_2 (b, MyIn, sel);
endmodule

module Not16 (
  input  [15:0] MyIn,
  output [15:0] MyOut
);

  assign MyOut = ~MyIn;  // NOT_Gate not_1, 16 bits wide
endmodule

module my_HA (
  input  a,
  input  b,
  output sum,
  output carry
);

  xor xor_1 (sum, a, b);
  and and_1 (carry, a, b);
endmodule

module my_FA (
  input  a,
  input  b,
  input  c,
  output sum,
  output carry
);

  wire and_1_out, and_2_out, and_3_out, and_4_out, xor_1_out;

  ExactlyOne xor_1 (.out(xor_1_out), .in0(a), .in1(b), .in2(c));
  and and_1 (and_1_out, a, b, c);
  and and_2 (and_2_out, b, c);
  and and_3 (and_3_out, c, a);
  and and_4 (and_4_out, a, b);
  or or_1 (carry, and_2_out, and_3_out, and_4_out);
  or or_2 (sum, xor_1_out, and_1_out);
endmodule

module my_FA2 (
  input  a,
  input  b,
  input  c,
  output sum,
  output carry
);

  wire my_ha_1_carry, my_ha_1_sum, my_ha_2_carry;

  my_HA my_ha_1 (.a(a), .b(b), .sum(my_ha_1_sum), .carry(my_ha_1_carry));
  my_HA my_ha_2 (.a(my_ha_1_sum), .b(c), .sum(sum), .carry(my_ha_2_carry));
  or or_1 (carry, my_ha_2_carry, my_ha_1_carry);
endmodule

module my_Add16 (
  input  [15:0] a,
  input  [15:0] b,
  output [15:0] sum
);

  wire adder_1_cout, adder_2_cout, adder_3_cout, adder_4_cout, adder_5_cout, adder_6_cout, adder_7_cout,
       adder_8_cout, adder_9_cout, adder_10_cout, adder_11_cout, adder_12_cout, adder_13_cout, adder_14_cout,
       adder_15_cout;

  Adder #(.width(1)) adder_1 (.a(a[0]), .b(b[0]), .out(sum[0]), .cout(adder_1_cout));  // open: cin
  Adder #(.width(1)) adder_2 (.a(a[1]), .b(b[1]), .out(sum[1]), .cin(adder_1_cout), .cout(adder_2_cout));
  Adder #(.width(1)) adder_3 (.a(a[2]), .b(b[2]), .out(sum[2]), .cin(adder_2_cout), .cout(adder_3_cout));
  Adder #(.width(1)) adder_4 (.a(a[3]), .b(b[3]), .out(sum[3]), .cin(adder_3_cout), .cout(adder_4_cout));
  Adder #(.width(1)) adder_5 (.a(a[4]), .b(b[4]), .out(sum[4]), .cin(adder_4_cout), .cout(adder_5_cout));
  Adder #(.width(1)) adder_6 (.a(a[5]), .b(b[5]), .out(sum[5]), .cin(adder_5_cout), .cout(adder_6_cout));
  Adder #(.width(1)) adder_7 (.a(a[6]), .b(b[6]), .out(sum[6]), .cin(adder_6_cout), .cout(adder_7_cout));
  Adder #(.width(1)) adder_8 (.a(a[7]), .b(b[7]), .out(sum[7]), .cin(adder_7_cout), .cout(adder_8_cout));
  Adder #(.width(1)) adder_9 (.a(a[8]), .b(b[8]), .out(sum[8]), .cin(adder_8_cout), .cout(adder_9_cout));
  Adder #(.width(1)) adder_10 (.a(a[9]), .b(b[9]), .out(sum[9]), .cin(adder_9_cout), .cout(adder_10_cout));
  Adder #(.width(1)) adder_11 (.a(a[10]), .b(b[10]), .out(sum[10]), .cin(adder_10_cout), .cout(adder_11_cout));
  Adder #(.width(1)) adder_12 (.a(a[11]), .b(b[11]), .out(sum[11]), .cin(adder_11_cout), .cout(adder_12_cout));
  Adder #(.width(1)) adder_13 (.a(a[12]), .b(b[12]), .out(sum[12]), .cin(adder_12_cout), .cout(adder_13_cout));
  Adder #(.width(1)) adder_14 (.a(a[13]), .b(b[13]), .out(sum[13]), .cin(adder_13_cout), .cout(adder_14_cout));
  Adder #(.width(1)) adder_15 (.a(a[14]), .b(b[14]), .out(sum[14]), .cin(adder_14_cout), .cout(adder_15_cout));
  Adder #(.width(1)) adder_16 (.a(a[15]), .b(b[15]), .out(sum[15]), .cin(adder_15_cout));  // open: cout
endmodule

module my_CLA4 (
  input  [3:0] a,
  input  [3:0] b,
  output [3:0] sum
);

  wire and_1_out, and_2_out, and_3_out, and_4_out, or_1_out, or_2_out, or_3_out;

  and and_1 (and_1_out, a[0], b[0]);
  and and_2 (and_2_out, a[1], b[1]);
  and and_3 (and_3_out, a[2], b[2]);
  and and_4 (and_4_out, a[3], b[3]);
  or or_1 (or_1_out, and_1_out, and_2_out);
  or or_2 (or_2_out, or_1_out, and_3_out);
  or or_3 (or_3_out, or_2_out, and_4_out);
  Adder #(.width(1)) adder_1 (.a(a[0]), .b(b[0]), .out(sum[0]));  // open: cin, cout
  Adder #(.width(1)) adder_2 (.a(a[1]), .b(b[1]), .out(sum[1]), .cin(or_1_out));  // open: cout
  Adder #(.width(1)) adder_3 (.a(a[2]), .b(b[2]), .out(sum[2]), .cin(or_2_out));  // open: cout
  Adder #(.width(1)) adder_4 (.a(a[3]), .b(b[3]), .out(sum[3]), .cin(or_3_out));  // open: cout
endmodule

module My_ALU (
  input  zx,
  input  nx,
  input  [15:0] x,
  input  f,
  input  no,
  input  [15:0] y,
  input  ny,
  input  zy,
  output [15:0] my_out,
  output zr,
  output ng
);

  wire or_1_out;
  wire [15:0] adder_1_out, and_1_out, and_2_out, and_3_out, multiplexer_1_out, multiplexer_2_out,
       multiplexer_3_out, multiplexer_4_out, multiplexer_5_out, not_1_out, not_2_out, not_3_out, not_4_out,
       not_5_out;

  assign not_1_out = ~x;  // NOT_Gate not_1, 16 bits wide
  assign not_2_out = ~y;  // NOT_Gate not_2, 16 bits wide
  assign and_1_out = x & not_1_out;  // AND_Gate and_1, 16 bits wide
  assign and_2_out = y & not_2_out;  // AND_Gate and_2, 16 bits wide
  Multiplexer #(.width(16)) multiplexer_1 (.in0(y), .in1(and_2_out), .out(multiplexer_1_out), .sel(zy));
  Multiplexer #(.width(16)) multiplexer_2 (.in0(x), .in1(and_1_out), .out(multiplexer_2_out), .sel(zx));
  assign not_3_out = ~multiplexer_1_out;  // NOT_Gate not_3, 16 bits wide
  Multiplexer #(.width(16)) multiplexer_3 (.in0(multiplexer_1_out), .in1(not_3_out), .out(multiplexer_3_out), .sel(ny));
  Multiplexer #(.width(16)) multiplexer_4 (.in0(multiplexer_2_out), .in1(not_4_out), .out(multiplexer_4_out), .sel(nx));
  assign not_4_out = ~multiplexer_2_out;  // NOT_Gate not_4, 16 bits wide
  assign and_3_out = multiplexer_4_out & multiplexer_3_out;  // AND_Gate and_3, 16 bits wide
  Adder #(.width(16)) adder_1 (.a(multiplexer_4_out), .b(multiplexer_3_out), .out(adder_1_out));  // open: cin, cout
  Multiplexer #(.width(16)) multiplexer_5 (.in0(and_3_out), .in1(adder_1_out), .out(multiplexer_5_out), .sel(f));
  Multiplexer #(.width(16)) multiplexer_6 (.in0(multiplexer_5_out), .in1(not_5_out), .out(my_out), .sel(no));
  assign not_5_out = ~multiplexer_5_out;  // NOT_Gate not_5, 16 bits wide
  or or_1 (or_1_out, my_out[0], my_out[1], my_out[2], my_out[3], my_out[4], my_out[5], my_out[6], my_out[7], my_out[8], my_out[9], my_out[10], my_out[11], my_out[12], my_out[13], my_out[14], my_out[15]);
  not not_6 (zr, or_1_out);

  assign ng = my_out[15];
endmodule

module My_ALU_Old (
  input  zx,
  input  [15:0] x,
  input  nx,
  input  zy,
  input  no,
  input  [15:0] y,
  input  f,
  input  ny,
  output [15:0] my_out,
  output ng,
  output zr
);

  wire and_1_out, and_2_out, and_3_out, and_4_out, and_5_out, and_6_out, and_7_out, and_8_out, and_9_out,
       and_10_out, and_11_out, and_12_out, and_13_out, and_14_out, and_15_out, and_16_out, and_17_out,
       and_18_out, and_19_out, and_20_out, and_21_out, and_22_out, and_23_out, and_24_out, and_25_out,
       and_26_out, and_27_out, and_28_out, and_29_out, and_30_out, and_31_out, and_32_out, not_1_out,
       not_2_out, or_1_out;
  wire [15:0] adder_1_out, and_33_out, multiplexer_1_out, xor_1_out, xor_17_out;

  not not_1 (not_1_out, zx);
  not not_2 (not_2_out, zy);
  and and_1 (and_1_out, x[0], not_1_out);
  and and_2 (and_2_out, x[1], not_1_out);
  and and_3 (and_3_out, x[2], not_1_out);
  and and_4 (and_4_out, x[3], not_1_out);
  and and_5 (and_5_out, x[4], not_1_out);
  and and_6 (and_6_out, x[5], not_1_out);
  and and_7 (and_7_out, x[6], not_1_out);
  and and_8 (and_8_out, x[7], not_1_out);
  and and_9 (and_9_out, x[8], not_1_out);
  and and_10 (and_10_out, x[9], not_1_out);
  and and_11 (and_11_out, x[10], not_1_out);
  and and_12 (and_12_out, x[11], not_1_out);
  and and_13 (and_13_out, x[12], not_1_out);
  and and_14 (and_14_out, x[13], not_1_out);
  and and_15 (and_15_out, x[14], not_1_out);
  and and_16 (and_16_out, x[15], not_1_out);
  and and_17 (and_17_out, y[0], not_2_out);
  and and_18 (and_18_out, y[1], not_2_out);
  and and_19 (and_19_out, y[2], not_2_out);
  and and_20 (and_20_out, y[3], not_2_out);
  and and_21 (and_21_out, y[4], not_2_out);
  and and_22 (and_22_out, y[5], not_2_out);
  and and_23 (and_23_out, y[6], not_2_out);
  and and_24 (and_24_out, y[7], not_2_out);
  and and_25 (and_25_out, y[8], not_2_out);
  and and_26 (and_26_out, y[9], not_2_out);
  and and_27 (and_27_out, y[10], not_2_out);
  and and_28 (and_28_out, y[11], not_2_out);
  and and_29 (and_29_out, y[12], not_2_out);
  and and_30 (and_30_out, y[13], not_2_out);
  and and_31 (and_31_out, y[14], not_2_out);
  and and_32 (and_32_out, y[15], not_2_out);
  xor xor_1 (xor_1_out[0], and_1_out, nx);
  xor xor_2 (xor_1_out[1], and_2_out, nx);
  xor xor_3 (xor_1_out[2], and_3_out, nx);
  xor xor_4 (xor_1_out[3], and_4_out, nx);
  xor xor_5 (xor_1_out[4], and_5_out, nx);
  xor xor_6 (xor_1_out[5], and_6_out, nx);
  xor xor_7 (xor_1_out[6], and_7_out, nx);
  xor xor_8 (xor_1_out[7], and_8_out, nx);
  xor xor_9 (xor_1_out[8], and_9_out, nx);
  xor xor_10 (xor_1_out[9], and_10_out, nx);
  xor xor_11 (xor_1_out[10], and_11_out, nx);
  xor xor_12 (xor_1_out[11], and_12_out, nx);
  xor xor_13 (xor_1_out[12], and_13_out, nx);
  xor xor_14 (xor_1_out[13], and_14_out, nx);
  xor xor_15 (xor_1_out[14], and_15_out, nx);
  xor xor_16 (xor_1_out[15], and_16_out, nx);
  xor xor_17 (xor_17_out[0], and_17_out, ny);
  xor xor_18 (xor_17_out[1], and_18_out, ny);
  xor xor_19 (xor_17_out[2], and_19_out, ny);
  xor xor_20 (xor_17_out[3], and_20_out, ny);
  xor xor_21 (xor_17_out[4], and_21_out, ny);
  xor xor_22 (xor_17_out[5], and_22_out, ny);
  xor xor_23 (xor_17_out[6], and_23_out, ny);
  xor xor_24 (xor_17_out[7], and_24_out, ny);
  xor xor_25 (xor_17_out[8], and_25_out, ny);
  xor xor_26 (xor_17_out[9], and_26_out, ny);
  xor xor_27 (xor_17_out[10], and_27_out, ny);
  xor xor_28 (xor_17_out[11], and_28_out, ny);
  xor xor_29 (xor_17_out[12], and_29_out, ny);
  xor xor_30 (xor_17_out[13], and_30_out, ny);
  xor xor_31 (xor_17_out[14], and_31_out, ny);
  xor xor_32 (xor_17_out[15], and_32_out, ny);
  assign and_33_out = xor_1_out & xor_17_out;  // AND_Gate and_33, 16 bits wide
  Adder #(.width(16)) adder_1 (.a(xor_1_out), .b(xor_17_out), .out(adder_1_out));  // open: cin, cout
  Multiplexer #(.width(16)) multiplexer_1 (.in0(and_33_out), .in1(adder_1_out), .out(multiplexer_1_out), .sel(f));
  xor xor_33 (my_out[0], multiplexer_1_out[0], no);
  xor xor_34 (my_out[1], multiplexer_1_out[1], no);
  xor xor_35 (my_out[2], multiplexer_1_out[2], no);
  xor xor_36 (my_out[3], multiplexer_1_out[3], no);
  xor xor_37 (my_out[4], multiplexer_1_out[4], no);
  xor xor_38 (my_out[5], multiplexer_1_out[5], no);
  xor xor_39 (my_out[6], multiplexer_1_out[6], no);
  xor xor_40 (my_out[7], multiplexer_1_out[7], no);
  xor xor_41 (my_out[8], multiplexer_1_out[8], no);
  xor xor_42 (my_out[9], multiplexer_1_out[9], no);
  xor xor_43 (my_out[10], multiplexer_1_out[10], no);
  xor xor_44 (my_out[11], multiplexer_1_out[11], no);
  xor xor_45 (my_out[12], multiplexer_1_out[12], no);
  xor xor_46 (my_out[13], multiplexer_1_out[13], no);
  xor xor_47 (my_out[14], multiplexer_1_out[14], no);
  xor xor_48 (my_out[15], multiplexer_1_out[15], no);
  or or_1 (or_1_out, my_out[15], my_out[14], my_out[13], my_out[12], my_out[11], my_out[10], my_out[9], my_out[8], my_out[7], my_out[6], my_out[5], my_out[4], my_out[3], my_out[2], my_out[1], my_out[0]);
  not not_3 (zr, or_1_out);

  assign ng = my_out[15];
endmodule

module my_Bit (
  input  load,
  input  my_in,
  output my_out
);

  wire and_1_out, and_2_out, clock_1_out;

  Clock clock_1 (.out(clock_1_out));
  and and_1 (and_1_out, load, my_in);
  and and_2 (and_2_out, load, clock_1_out);
  D_Flip_Flop #(.trigger("falling")) d_ff_1 (.D(and_1_out), .clk(and_2_out), .Q(my_out));  // open: Qn, preset, reset
endmodule
